# Fritzing sketch projet (saved by Fritzing 0.9.5d)
circuit board: 8.46667cm x 5.64444cm
breadboards: 1

parts:
  Composant1 = Arduino Uno (Rev3)
  LED1 = LED - 5mm [color="Orange (620nm)" package="5 mm [THT]"]
  R1 = Resistor [tolerance=±5% resistance=220 package=THT]
  R2 = Rotary Potentiometer (Small) [maximum_resistance=100kΩ package=THT]

nets:
  N1: Composant1.A0, R2.wiper
  N2: Composant1.A1, LED1.anode
  N3: Composant1.5V, R2.leg2
  N4: Composant1.GND, R1.Pin_1, R2.leg1
  N5: LED1.cathode, R1.Pin_0
